// Logisim project report.circ as structural Verilog: 2 circuits, main circuit main
module main (
  input  in_1,
  input  in_2,
  input  in_3,
  input  in_4,
  input  in_5,
  input  in_6,
  input  in_7,
  input  in_8
);

  wire AC, and_1_out, and_2_out, and_3_out, and_4_out, and_6_out, and_8_out, and_9_out, and_10_out,
       and_11_out, and_12_out, and_14_out, AR, clock_1_out, D0, D1, D2, D3, D4, D5, D6, D7, DR, I, INCPC, IR,
       nor_1_out, not_1_out, or_2_out, or_5_out, or_7_out, or_9_out, PC, READ, SC, T0, T1, T2, T3, T4, T5,
       T6, T7, TR, WRITE;
  wire [2:0] ALU, BUS, Bus_t, IR_q_2;
  wire [3:0] counter_1_q;
  wire [6:0] AR_q, bit_extender_2_out, bit_extender_3_out, PC_q;
  wire [11:0] IR_q;
  wire [15:0] AC_q, ADRESS, alu_1_out, bit_extender_4_out, bit_extender_5_out, DR_q, multiplexer_1_out,
       ram_1_data, TR_q;

  alu alu_1 (.A(DR_q), .B(AC_q), .in_2(ALU), .out(alu_1_out));
  Decoder #(.select(4)) decoder_1 (
    .out0(T0), .out1(T1), .out2(T2), .out3(T3), .out4(T4), .out5(T5), .out6(T6), .out7(T7), .sel(counter_1_q));  // open: out8, out9, out10, out11, out12, out13, out14, out15, en
  Clock clock_1 (.out(clock_1_out));
  Decoder #(.select(3)) decoder_2 (
    .out0(D0), .out1(D1), .out2(D2), .out3(D3), .out4(D4), .out5(D5), .out6(D6), .out7(D7), .sel(IR_q_2),
    .en(T2));
  not not_1 (not_1_out, SC);
  assign ADRESS = {{4{1'b0}}, IR_q};  // Bit_Extender bit_extender_1
  Bit_Extender #(.in_width(16), .out_width(7)) bit_extender_2 (.in(multiplexer_1_out), .out(bit_extender_2_out));
  Bit_Extender #(.in_width(16), .out_width(7)) bit_extender_3 (.in(multiplexer_1_out), .out(bit_extender_3_out));
  Counter #(.width(4), .max('h8)) counter_1 (
    .count(not_1_out), .Q(counter_1_q), .clk(clock_1_out), .clr(SC));  // open: load, D, carry
  Register #(.width(7)) u_AR (.D(bit_extender_2_out), .en(AR), .Q(AR_q), .clk(clock_1_out));  // open: clr
  Counter #(.width(7), .max('h7f)) u_PC (
    .load(PC), .D(bit_extender_3_out), .count(INCPC), .Q(PC_q), .clk(clock_1_out));  // open: carry, clr
  Register #(.width(16)) u_AC (.D(alu_1_out), .Q(AC_q), .clk(clock_1_out));  // open: en, clr
  Register #(.width(16)) u_DR (.D(multiplexer_1_out), .Q(DR_q), .clk(clock_1_out));  // open: en, clr
  Register #(.width(16)) u_TR (.D(multiplexer_1_out), .en(TR), .Q(TR_q), .clk(clock_1_out));  // open: clr
  Register #(.width(16)) u_IR (.D(multiplexer_1_out), .en(IR), .Q({I, IR_q_2, IR_q}), .clk(clock_1_out));  // open: clr
  assign bit_extender_4_out = {{9{1'b0}}, PC_q};  // Bit_Extender bit_extender_4
  RAM #(.addrWidth(7), .dataWidth(16), .bus("separate")) ram_1 (
    .addr(AR_q), .din(multiplexer_1_out), .data(ram_1_data), .str(WRITE), .clk(clock_1_out), .ld(READ),
    .clr(in_1));  // open: sel
  assign bit_extender_5_out = {{9{1'b0}}, AR_q};  // Bit_Extender bit_extender_5
  or or_1 (READ, T1, and_1_out);
  and and_1 (and_1_out, T4, or_9_out);
  Multiplexer #(.select(3), .width(16), .enable("false")) multiplexer_1 (
    .in0(ram_1_data), .in1(bit_extender_5_out), .in2(bit_extender_4_out), .in3(AC_q), .in4(DR_q), .in5(TR_q),
    .in7({I, IR_q_2, IR_q}), .out(multiplexer_1_out), .sel(BUS));  // open: in6
  or or_2 (or_2_out, T4, D4);
  and and_2 (and_2_out, T4, D3);
  or or_3 (WRITE, and_2_out, and_3_out);
  and and_3 (and_3_out, T6, D6);
  and and_4 (and_4_out, T5, or_5_out);
  or or_4 (PC, T4, D4);
  or or_5 (or_5_out, D3, D4);
  or or_6 (AR, T0, T2);
  Priority_Encoder priority_encoder_1 (
    .in0(READ), .in1(or_2_out), .in2(T0), .in3(WRITE), .in4(in_6), .in5(in_7), .in7(in_8), .out(Bus_t));  // open: in6, en_in, gs, en_out
  and and_5 (SC, and_4_out, and_6_out);
  and and_6 (and_6_out, T5, or_7_out);
  or or_7 (or_7_out, D5, D2, D1, D0);
  and and_7 (DR, T4, or_9_out);
  or or_8 (INCPC, T1, and_11_out);
  and and_8 (and_8_out, D2, T5);
  and and_9 (and_9_out, T5, D6);
  and and_10 (and_10_out, T5, D5);
  and and_11 (and_11_out, nor_1_out, T7, D7);
  nor nor_1 (nor_1_out, DR, in_2);
  and and_12 (and_12_out, T5, D0);
  and and_13 (AC, T5, or_9_out);
  or or_9 (or_9_out, D6, D2, D5, D1, D0);
  and and_14 (and_14_out, T5, D1);
  Priority_Encoder priority_encoder_2 (
    .in0(in_3), .in1(and_8_out), .in2(and_9_out), .in3(and_10_out), .in4(in_4), .in5(and_12_out),
    .in6(and_14_out), .in7(in_5), .out(ALU));  // open: en_in, gs, en_out
endmodule

// ALU
module alu (
  input  [15:0] A,
  input  [2:0] in_2,
  input  [15:0] B,
  output [15:0] out
);

  wire [15:0] adder_1_out, adder_2_out, divider_1_out, multiplier_1_out, subtractor_1_out, xor_1_out;

  Adder #(.width(16)) adder_1 (.a(A), .b(16'h1), .out(adder_1_out));  // open: cin, cout
  Multiplier #(.width(16)) multiplier_1 (.a(A), .b(B), .out(multiplier_1_out));  // open: cin, cout
  Divider #(.width(16)) divider_1 (.a(A), .b(B), .out(divider_1_out));  // open: upper, rem
  Subtractor #(.width(16)) subtractor_1 (.a(A), .b(B), .out(subtractor_1_out));  // open: bin, bout
  Adder #(.width(16)) adder_2 (.a(A), .b(B), .out(adder_2_out));  // open: cin, cout
  assign xor_1_out = A ^ B;  // XOR_Gate xor_1, 16 bits wide
  Multiplexer #(.select(3), .width(16), .enable("false")) multiplexer_1 (
    .in1(A), .in2(adder_1_out), .in3(multiplier_1_out), .in4(subtractor_1_out), .in5(divider_1_out),
    .in6(adder_2_out), .in7(xor_1_out), .out(out), .sel(in_2));  // open: in0
endmodule
